# Fritzing sketch autoRC UNO r4 WIFI - fritzing (saved by Fritzing 0.9.10b)
breadboards: 1

parts:
  Encoder_Izquierdo = shaft encoder
  C1 = Electrolytic Capacitor [capacitance=100nF voltage=35V package="100 mil [THT, electrolytic]"]  # not connected
  Encoder_Derecho = shaft encoder
  C2 = Electrolytic Capacitor [capacitance=100nF voltage=35V package="100 mil [THT, electrolytic]"]  # not connected
  S1 = H-Bridge with L298N
  TRASERA_DERECHA = gear-motor
  DELANTERA_DERECHA = gear-motor
  HC-SR04_Sensor_1 = HC-SR04 Ultrasonic Distance Sensor
  A1 = Arduino UNO R4 WiFi
  BAT1 = Battery Holders [package=battery-aa-kit]  # not connected
  TRASERA_IZQDA = gear-motor
  DELANTERA_IZDA = gear-motor
  J1 = Basic Servo
  C3 = Electrolytic Capacitor [capacitance=100nF voltage=35V package="100 mil [THT, electrolytic]"]  # not connected

nets:
  N1: Encoder_Izquierdo.OUT, A1.Pin_37
  N2: Encoder_Derecho.OUT, A1.Pin_36
  N3: S1.ENA, A1.Pin_40
  N4: S1.IN1, A1.Pin_38
  N5: S1.IN2, A1.Pin_39
  N6: S1.IN3, A1.Pin_41
  N7: S1.IN4, A1.Pin_42
  N8: S1.ENB, A1.Pin_43
  N9: S1.M1-01, TRASERA_IZQDA.pin_2, DELANTERA_IZDA.pin_2
  N10: S1.M1-02, TRASERA_IZQDA.pin_1, DELANTERA_IZDA.pin_1
  N11: S1.M2-01, TRASERA_DERECHA.pin_2, DELANTERA_DERECHA.pin_2
  N12: S1.M2-02, TRASERA_DERECHA.pin_1, DELANTERA_DERECHA.pin_1
  N13: HC-SR04_Sensor_1.TRIG, A1.Pin_47
  N14: HC-SR04_Sensor_1.ECHO, A1.Pin_46
  N15: A1.Pin_44, J1.pulse

notes:
  OUT1 rojo
  OUT2 GND
  OUT3 rojo
  OUT4 GND
  5v

custom parts:
  H-Bridge with L298N: h-bridge
  gear-motor: Generic gear motor, 3V to 6V, dual output shafts, 1:48 gear ratio.
  Arduino UNO R4 WiFi: The Arduino UNO R4 WiFi merges the RA4M1 microprocessor from Renesas with the ESP32-S3 from Espressif, creating an all-in-one tool for makers with enhanced processing power and a diverse array of new peripherals.
